// Logisim project b4_group.circ as structural Verilog: 3 circuits, main circuit main
module main (
  input  A4,
  input  A3,
  input  A2,
  input  A1,
  input  B4,
  input  B3,
  input  B2,
  input  B1,
  input  S2,
  input  S1,
  input  S0,
  input  in_12,
  input  in_13,
  output C,
  output S,
  output V,
  output Z,
  output F4,
  output F3,
  output F2,
  output F1
);

  wire n7404_1_p2, n7404_1_p4, n7404_1_p6, n7404_1_p8, n7404_1_p9, n7404_2_p2, n7404_2_p4, n7404_2_p6,
       n7404_2_p8, n7404_2_p9, n7408_1_p3, n7408_1_p6, n7408_1_p10, n7408_1_p13, n7408_2_p3, n7432_1_p3,
       n7432_1_p6, n7432_1_p9, n7432_2_p3, n7432_2_p8, n7432_2_p11, n7483_1_p2, n7483_1_p5, n7483_1_p9,
       n7483_1_p10, n7483_1_p11, n7483_1_p14, n7486_1_p6, n7486_1_p9, n7486_1_p12, n74157_1_p2, n74157_1_p5,
       n74157_1_p9, n74157_1_p12;

  // _7404 7404_1: pin names not known; wires that end beside it: B4, n7404_1_p2, B3, n7404_1_p4, B2, n7404_1_p6, B1, n7404_1_p8, n7404_1_p9
  // _7408 7408_1: pin names not known; wires that end beside it: n7404_1_p2, S1, n7408_1_p3, n7404_1_p4, S1, n7408_1_p6, Z, S1, n7404_1_p8, n7408_1_p10, S1, n7404_1_p6, n7408_1_p13
  // _7483 7483_1: pin names not known; wires that end beside it: A4, n7483_1_p2, A3, n7408_1_p6, n7483_1_p5, n7408_1_p13, A2, n7408_1_p3, n7483_1_p9, n7483_1_p10, n7483_1_p11, n7408_1_p10, A1, n7483_1_p14
  // _7486 7486_1: pin names not known; wires that end beside it: S2, S1, n7483_1_p11, n7483_1_p9, A4, n7486_1_p6, n7486_1_p6, B4, n7486_1_p9, n7486_1_p9, n7483_1_p10, n7486_1_p12
  // _7432 7432_1: pin names not known; wires that end beside it: F4, F3, n7432_1_p3, n7432_1_p3, F2, n7432_1_p6, S1, S2, n7432_1_p9, F1, n7432_1_p6, n7404_1_p9
  // _74157 74157_1: pin names not known; wires that end beside it: S0, n74157_1_p2, n7483_1_p9, F4, n74157_1_p5, n7483_1_p2, F3, in_13, n74157_1_p9, n7483_1_p14, F1, n74157_1_p12, n7483_1_p5, F2
  // _7408 7408_2: pin names not known; wires that end beside it: S0, n7432_1_p9, n7408_2_p3, n7408_2_p3, n7486_1_p12, V, n7408_2_p3, n7483_1_p10, C
  // _7404 7404_2: pin names not known; wires that end beside it: A4, n7404_2_p2, A3, n7404_2_p4, A2, n7404_2_p6, A1, n7404_2_p8, n7404_2_p9
  // _7432 7432_2: pin names not known; wires that end beside it: A4, B4, n7432_2_p3, A3, B3, B2, A2, n7432_2_p8, B1, A1, n7432_2_p11, B1, B2, B3, B4, A1, A2, A3, A4
  // _74157 74157_2: pin names not known; wires that end beside it: S1, n7432_2_p3, n7404_2_p2, n74157_1_p2, n7404_2_p9, n7404_2_p4, n74157_1_p5, in_12, n7432_2_p11, n7404_2_p8, n74157_1_p9, n7432_2_p8, n7404_2_p6, n74157_1_p12

  assign S = F4;
endmodule

module _74158 (
  input  S,
  input  E,
  input  A1,
  input  A4,
  input  B1,
  input  B4,
  input  A2,
  input  A3,
  input  B2,
  input  B3,
  output Y1,
  output Y4,
  output Y2,
  output Y3
);

  wire n74157_1_p6, n74157_1_p9, n74157_1_p13, n74157_1_p16;

  not not_1 (Y1, n74157_1_p6);
  not not_2 (Y2, n74157_1_p9);
  // _74157 74157_1: pin names not known; wires that end beside it: Y2, Y1, S, A1, B1, n74157_1_p6, A2, B2, n74157_1_p9, E, A4, B4, n74157_1_p13, A3, B3, n74157_1_p16, Y4
  not not_3 (Y4, n74157_1_p13);
  not not_4 (Y3, n74157_1_p16);
endmodule

module main2 (
  input  A4,
  input  A3,
  input  A2,
  input  A1,
  input  B4,
  input  B3,
  input  B2,
  input  B1,
  input  S2,
  input  S1,
  input  S0,
  input  in_12,
  input  in_13,
  input  in_14,
  input  in_15,
  output C,
  output S,
  output V,
  output Z,
  output F4,
  output F3,
  output F2,
  output F1
);

  wire n7404_1_p4, n7404_1_p6, n7404_1_p8, n7404_1_p10, n7408_1_p3, n7432_1_p3, n7432_1_p6, n7432_1_p9,
       n7432_1_p12, n7432_2_p3, n7432_2_p6, n7432_2_p9, n7432_2_p12, n7483_1_p2, n7483_1_p5, n7483_1_p9,
       n7483_1_p10, n7483_1_p11, n7483_1_p14, n7486_1_p6, n7486_1_p9, n7486_1_p12, n74157_1_p2, n74157_1_p5,
       n74157_1_p9, n74157_1_p12, n74158_1_y1, n74158_1_y2, n74158_1_y3, n74158_1_y4;

  _74158 u_74158_1 (
    .S(S1), .A1(in_13), .B1(B4), .Y1(n74158_1_y1), .A2(in_13), .B2(B3), .Y2(n74158_1_y2), .E(in_12),
    .A4(in_13), .B4(B2), .Y4(n74158_1_y4), .A3(in_13), .B3(B1), .Y3(n74158_1_y3));
  // _7483 7483_1: pin names not known; wires that end beside it: A4, n7483_1_p2, A3, n74158_1_y2, n7483_1_p5, n74158_1_y4, A2, n74158_1_y1, n7483_1_p9, n7483_1_p10, n7483_1_p11, n74158_1_y3, A1, n7483_1_p14
  // _7486 7486_1: pin names not known; wires that end beside it: S2, S1, n7483_1_p11, n7483_1_p9, A4, n7486_1_p6, n7486_1_p6, n74158_1_y1, n7486_1_p9, n7486_1_p9, n7483_1_p10, n7486_1_p12
  // _7432 7432_1: pin names not known; wires that end beside it: F4, F3, n7432_1_p3, n7432_1_p3, F2, n7432_1_p6, S1, S2, n7432_1_p9, F1, n7432_1_p6, n7432_1_p12
  // _74157 74157_1: pin names not known; wires that end beside it: S0, n74157_1_p2, n7483_1_p9, F4, n74157_1_p5, n7483_1_p2, F3, in_15, n74157_1_p9, n7483_1_p14, F1, n74157_1_p12, n7483_1_p5, F2
  // _7408 7408_1: pin names not known; wires that end beside it: S0, n7432_1_p9, n7408_1_p3, n7408_1_p3, n7486_1_p12, V, n7408_1_p3, n7483_1_p10, C
  // _7404 7404_1: pin names not known; wires that end beside it: n7432_1_p12, Z, A3, n7404_1_p4, A2, n7404_1_p6, A1, n7404_1_p8, A4, n7404_1_p10
  // _7432 7432_2: pin names not known; wires that end beside it: A4, B4, n7432_2_p3, A3, B3, n7432_2_p6, B2, A2, n7432_2_p9, B1, A1, n7432_2_p12, B1, B2, B3, B4, A1, A2, A3, A4
  // _74157 74157_2: pin names not known; wires that end beside it: S1, n7432_2_p3, n7404_1_p10, n74157_1_p2, n7432_2_p6, n7404_1_p4, n74157_1_p5, in_14, n7432_2_p12, n7404_1_p8, n74157_1_p9, n7432_2_p9, n7404_1_p6, n74157_1_p12

  assign S = F4;
endmodule
