// Logisim project B2_Group4.circ as structural Verilog: 13 circuits, main circuit main
module main (
  input  [31:0] InputA,
  input  [31:0] Input_B,
  output [31:0] Output,
  output underFlow,
  output Overflow
);

  FloatAdder floatadder_1 (
    .Input_A(InputA), .Input_B(Input_B), .Output(Output), .Overflow(Overflow), .Underflow(underFlow));

  // Notes on the sheet:
  //   B2_Group4
  //   1905095,106,110,111,113
endmodule

module FloatSpliter (
  input  [31:0] Input,
  output [31:0] Significand,
  output [11:0] Exponent,
  output Sign
);

  BitFinder #(.width(12)) bitfinder_1 (.in(Input[30:19]), .found(Significand[30]));  // open: index

  assign Exponent = Input[30:19];
  assign Sign = Input[31];
  assign {Significand[31], Significand[29:0]} = {1'b0, Input[18:0], {11{1'b0}}};
endmodule

module Aligner (
  input  [31:0] Significand_A,
  input  [31:0] Significand_B,
  input  [11:0] Exponent_A,
  input  [11:0] Exponent_B,
  input  Sign_A,
  input  Sign_B,
  output [31:0] Unshifted_Significand,
  output [31:0] Shifted_Significand,
  output [11:0] Exp_Out,
  output Unshifted_Sign,
  output Shifted_Sign
);

  wire bitfinder_1_found, subtractor_1_bout;
  wire [11:0] n12_bit_mux_1_out_4, negator_1_out, subtractor_1_out;
  wire [31:0] n32bit_mux_2_out, shifter_1_out;

  Subtractor #(.width(12)) subtractor_1 (
    .a(Exponent_A), .b(Exponent_B), .out(subtractor_1_out), .bout(subtractor_1_bout));  // open: bin
  Negator #(.width(12)) negator_1 (.in(subtractor_1_out), .out(negator_1_out));
  _1_bit_mux u_1_bit_mux_1 (._0(Sign_A), .s(subtractor_1_bout), ._1(Sign_B), .out(Unshifted_Sign));
  _32bit_mux u_32bit_mux_1 (._0(Significand_A), .s(subtractor_1_bout), ._1(Significand_B), .out(Unshifted_Significand));
  _32bit_mux u_32bit_mux_2 (._0(Significand_B), .s(subtractor_1_bout), ._1(Significand_A), .out(n32bit_mux_2_out));
  _12_bit_mux u_12_bit_mux_1 (
    .in_1(subtractor_1_out), .S(subtractor_1_bout), .in_3(negator_1_out), .out_4(n12_bit_mux_1_out_4));
  _12_bit_mux u_12_bit_mux_2 (.in_1(Exponent_A), .S(subtractor_1_bout), .in_3(Exponent_B), .out_4(Exp_Out));
  _1_bit_mux u_1_bit_mux_2 (._0(Sign_B), .s(subtractor_1_bout), ._1(Sign_A), .out(Shifted_Sign));
  Shifter #(.width(32), .shift("lr")) shifter_1 (
    .in(n32bit_mux_2_out), .\dist (n12_bit_mux_1_out_4[4:0]), .out(shifter_1_out));
  BitFinder #(.width(7)) bitfinder_1 (.in(n12_bit_mux_1_out_4[11:5]), .found(bitfinder_1_found));  // open: index
  _32bit_mux u_32bit_mux_3 (._0(shifter_1_out), .s(bitfinder_1_found), ._1({32{1'b0}}), .out(Shifted_Significand));
endmodule

module SignificandAdder (
  input  [31:0] Significand_A,
  input  Sign_A,
  input  [31:0] Significand_B,
  input  Sign_B,
  output [31:0] Resultant_Significand,
  output Resultant_Sign
);

  wire comparator_1_lt, n1_bit_mux_1_out, n7486_1_p3;
  wire [31:0] adder_1_out, n32bit_mux_1_out, n32bit_mux_2_out, negator_1_out, negator_2_out, negator_3_out;

  Negator #(.width(32)) negator_1 (.in(Significand_A), .out(negator_1_out));
  Comparator #(.width(32), .mode("unsigned")) comparator_1 (
    .a(Significand_A), .b(Significand_B), .lt(comparator_1_lt));  // open: gt, eq
  Negator #(.width(32)) negator_2 (.in(Significand_B), .out(negator_2_out));
  _32bit_mux u_32bit_mux_1 (._0(Significand_A), .s(Sign_A), ._1(negator_1_out), .out(n32bit_mux_1_out));
  _32bit_mux u_32bit_mux_2 (._0(Significand_B), .s(Sign_B), ._1(negator_2_out), .out(n32bit_mux_2_out));
  Adder #(.width(32)) adder_1 (.a(n32bit_mux_1_out), .b(n32bit_mux_2_out), .out(adder_1_out));  // open: cin, cout
  // _7486 7486_1: pin names not known; wires that end beside it: Sign_A, Sign_B, n7486_1_p3
  Negator #(.width(32)) negator_3 (.in(adder_1_out), .out(negator_3_out));
  _1_bit_mux u_1_bit_mux_1 (._0(Sign_A), .s(comparator_1_lt), ._1(Sign_B), .out(n1_bit_mux_1_out));
  _32bit_mux u_32bit_mux_3 (._0(adder_1_out), .s(Resultant_Sign), ._1(negator_3_out), .out(Resultant_Significand));
  _1_bit_mux u_1_bit_mux_2 (._0(Sign_A), .s(n7486_1_p3), ._1(n1_bit_mux_1_out), .out(Resultant_Sign));
endmodule

module FloatAdder (
  input  [31:0] Input_A,
  input  [31:0] Input_B,
  output [31:0] Output,
  output Overflow,
  output Underflow
);

  wire Aligner_shifted_sign, Aligner_unshifted_sign, FloatSpliter_2_sign, FloatSpliter_sign,
       Normalizer_overflow, Rounder_overflow;
  wire [11:0] Aligner_exp_out, FloatSpliter_2_exponent, FloatSpliter_exponent, Normalizer_exponent_2;
  wire [31:0] Aligner_shifted_significand, Aligner_unshifted_significand, FloatSpliter_2_significand,
       FloatSpliter_significand, Normalizer_significand_2, SignificandAdder_resultant_significand;

  FloatSpliter FloatSpliter (
    .Input(Input_A), .Significand(FloatSpliter_significand), .Exponent(FloatSpliter_exponent),
    .Sign(FloatSpliter_sign));
  FloatSpliter FloatSpliter_2 (
    .Input(Input_B), .Significand(FloatSpliter_2_significand), .Exponent(FloatSpliter_2_exponent),
    .Sign(FloatSpliter_2_sign));
  Aligner Aligner (
    .Significand_A(FloatSpliter_significand), .Significand_B(FloatSpliter_2_significand),
    .Exponent_A(FloatSpliter_exponent), .Exponent_B(FloatSpliter_2_exponent), .Sign_A(FloatSpliter_sign),
    .Sign_B(FloatSpliter_2_sign), .Unshifted_Significand(Aligner_unshifted_significand),
    .Shifted_Significand(Aligner_shifted_significand), .Exp_Out(Aligner_exp_out),
    .Unshifted_Sign(Aligner_unshifted_sign), .Shifted_Sign(Aligner_shifted_sign));
  Normalizer Normalizer (
    .Significand(SignificandAdder_resultant_significand), .exponent(Aligner_exp_out),
    .significand_2(Normalizer_significand_2), .exponent_2(Normalizer_exponent_2),
    .overflow(Normalizer_overflow), .underflow(Underflow));
  SignificandAdder SignificandAdder (
    .Significand_A(Aligner_unshifted_significand), .Sign_A(Aligner_unshifted_sign),
    .Significand_B(Aligner_shifted_significand), .Sign_B(Aligner_shifted_sign),
    .Resultant_Significand(SignificandAdder_resultant_significand), .Resultant_Sign(Output[31]));
  Rounder Rounder (
    .ExpoIn(Normalizer_exponent_2), .ExpoOut(Output[30:19]), .SigIn(Normalizer_significand_2),
    .SigOut(Output[18:0]), .overflow(Rounder_overflow));
  // _7432 7432_1: pin names not known; wires that end beside it: Overflow, Rounder_overflow, Normalizer_overflow
endmodule

module reverseBit (
  input  [30:0] Input,
  output [30:0] Reversed_output
);


  assign Reversed_output = {Input[0], Input[1], Input[2], Input[3], Input[4], Input[5], Input[6], Input[7], Input[8], Input[9], Input[10], Input[11], Input[12], Input[13], Input[14], Input[15], Input[16], Input[17], Input[18], Input[19], Input[20], Input[21], Input[22], Input[23], Input[24], Input[25], Input[26], Input[27], Input[28], Input[29], Input[30]};
endmodule

module Normalizer (
  input  [31:0] Significand,
  input  [11:0] exponent,
  output [31:0] significand_2,
  output [11:0] exponent_2,
  output overflow,
  output underflow
);

  wire bitfinder_4_found, n7404_1_p1, n7404_1_p5, n7408_1_p2, n7432_1_p1, n7432_1_p2, n7432_1_p3;
  wire [4:0] bit_extender_2_out, bitfinder_3_index;
  wire [11:0] bit_extender_1_out, n12_bit_mux_1_out_4, subtractor_1_out;
  wire [30:0] reversebit_1_reversed_output;
  wire [31:0] shifter_1_out, shifter_2_out;

  // _7432 7432_1: pin names not known; wires that end beside it: n7432_1_p1, n7432_1_p2, n7432_1_p3
  // _7408 7408_1: pin names not known; wires that end beside it: n7432_1_p1, n7408_1_p2, underflow, Significand[31]
  // _7404 7404_1: pin names not known; wires that end beside it: n7404_1_p1, overflow, Significand[31], n7408_1_p2, n7404_1_p5, n7432_1_p2
  assign bit_extender_1_out = {{11{Significand[31]}}, Significand[31]};  // Bit_Extender bit_extender_1
  _12_bit_mux u_12_bit_mux_1 (
    .in_1({{7{1'b0}}, bitfinder_3_index}), .S(Significand[31]), .in_3(bit_extender_1_out),
    .out_4(n12_bit_mux_1_out_4));
  BitFinder #(.width(12), .\type ("low0")) bitfinder_1 (.in(subtractor_1_out), .found(n7404_1_p1));  // open: index
  assign bit_extender_2_out = {{4{1'b0}}, Significand[31]};  // Bit_Extender bit_extender_2
  Subtractor #(.width(12)) subtractor_1 (
    .a(exponent), .b(n12_bit_mux_1_out_4), .out(subtractor_1_out), .bin(1'b0), .bout(n7432_1_p3));
  BitFinder #(.width(12)) bitfinder_2 (.in(subtractor_1_out), .found(n7404_1_p5));  // open: index
  Shifter #(.width(32), .shift("lr")) shifter_1 (.in(Significand), .\dist (bit_extender_2_out), .out(shifter_1_out));
  reverseBit reversebit_1 (.Input(Significand[30:0]), .Reversed_output(reversebit_1_reversed_output));
  BitFinder #(.width(31)) bitfinder_3 (.in(reversebit_1_reversed_output), .index(bitfinder_3_index));  // open: found
  Shifter #(.width(32)) shifter_2 (.in(Significand), .\dist (bitfinder_3_index), .out(shifter_2_out));
  BitFinder #(.width(32)) bitfinder_4 (.in(significand_2), .found(bitfinder_4_found));  // open: index
  _12_bit_mux u_12_bit_mux_2 (.in_1({12{1'b0}}), .S(bitfinder_4_found), .in_3(subtractor_1_out), .out_4(exponent_2));
  _32bit_mux u_32bit_mux_1 (._0(shifter_2_out), .s(Significand[31]), ._1(shifter_1_out), .out(significand_2));
endmodule

module Rounder (
  input  [11:0] ExpoIn,
  input  [31:0] SigIn,
  output [11:0] ExpoOut,
  output overflow,
  output [18:0] SigOut
);

  wire bitfinder_2_found, n7408_1_p3, n7432_1_p3, n7432_1_p5, n7432_1_p6;
  wire [4:0] bit_extender_1_out;
  wire [20:0] adder_2_out;
  wire [20:19] shifter_1_out;

  Adder #(.width(12)) adder_1 (.a(ExpoIn), .b({12{1'b0}}), .out(ExpoOut), .cin(adder_2_out[20]));  // open: cout
  // _7432 7432_1: pin names not known; wires that end beside it: SigIn[11], SigIn[9], n7432_1_p3, n7432_1_p3, n7432_1_p5, n7432_1_p6
  Adder #(.width(21)) adder_2 (.a(SigIn[31:11]), .b({21{1'b0}}), .out(adder_2_out), .cin(n7408_1_p3));  // open: cout
  BitFinder #(.width(9)) bitfinder_1 (.in(SigIn[8:0]), .found(n7432_1_p5));  // open: index
  assign bit_extender_1_out = {{4{1'b0}}, adder_2_out[20]};  // Bit_Extender bit_extender_1
  // _7408 7408_1: pin names not known; wires that end beside it: n7432_1_p6, SigIn[10], n7408_1_p3
  Shifter #(.width(21), .shift("lr")) shifter_1 (
    .in(adder_2_out), .\dist (bit_extender_1_out), .out({shifter_1_out, SigOut}));
  BitFinder #(.width(12), .\type ("low0")) bitfinder_2 (.in(ExpoOut), .found(bitfinder_2_found));  // open: index
  // _7404 7404_1: pin names not known; wires that end beside it: overflow, bitfinder_2_found

  // Notes on the sheet:
  //   S = 0-8, R = 9, G = 10, C D FRAC = 31-11
  //   K
  //   C
  //   S
  //   G(R+S+K)
  //   D,FRAC = 21,20-0
endmodule

module _4_bit_mux (
  input  [3:0] _0,
  input  select,
  input  [3:0] _1,
  output [3:0] out
);

  // _74157 74157_1: pin names not known; wires that end beside it: select, _0[0], _1[0], out[0], _0[1], _1[1], out[1], 1'b0, _0[3], _1[3], out[3], _0[2], _1[2], out[2]
endmodule

module _8_bit_mux (
  input  [7:0] _0,
  input  s,
  input  [7:0] _1,
  output [7:0] out
);

  _4_bit_mux u_4_bit_mux_1 (._0(_0[3:0]), .select(s), ._1(_1[3:0]), .out(out[3:0]));
  _4_bit_mux u_4_bit_mux_2 (._0(_0[7:4]), .select(s), ._1(_1[7:4]), .out(out[7:4]));
endmodule

module _32bit_mux (
  input  [31:0] _0,
  input  s,
  input  [31:0] _1,
  output [31:0] out
);

  _8_bit_mux u_8_bit_mux_1 (._0(_0[7:0]), .s(s), ._1(_1[7:0]), .out(out[7:0]));
  _8_bit_mux u_8_bit_mux_2 (._0(_0[15:8]), .s(s), ._1(_1[15:8]), .out(out[15:8]));
  _8_bit_mux u_8_bit_mux_3 (._0(_0[23:16]), .s(s), ._1(_1[23:16]), .out(out[23:16]));
  _8_bit_mux u_8_bit_mux_4 (._0(_0[31:24]), .s(s), ._1(_1[31:24]), .out(out[31:24]));
endmodule

module _12_bit_mux (
  input  [11:0] in_1,
  input  S,
  input  [11:0] in_3,
  output [11:0] out_4
);

  _8_bit_mux u_8_bit_mux_1 (._0(in_1[7:0]), .s(S), ._1(in_3[7:0]), .out(out_4[7:0]));
  _4_bit_mux u_4_bit_mux_1 (._0(in_1[11:8]), .select(S), ._1(in_3[11:8]), .out(out_4[11:8]));
endmodule

module _1_bit_mux (
  input  _0,
  input  s,
  input  _1,
  output out
);

  // _74157 74157_1: pin names not known; wires that end beside it: s, _0, _1, out, 1'b0
endmodule
