// Logisim project B2_Group4.circ as structural Verilog: 2 circuits, main circuit main
module main (
  input  in_1,
  input  Data_Memory,
  input  in_3,
  input  in_4,
  output [3:0] out_5,
  output [3:0] to,
  output [3:0] t1,
  output [3:0] t2,
  output [3:0] t3,
  output [3:0] t4,
  output [3:0] sp
);

  wire branch_1_branch, comparator_1_eq, main_1_p3, main_1_p4, main_1_p5, main_1_p6, main_1_p7, main_1_p8,
       main_1_p9, main_1_p10, main_1_p11, main_1_p12, main_2_p2, not_1_out, registerfile_1_p13;
  wire [3:0] main_2_p4, multiplexer_3_out, multiplexer_4_out, multiplexer_5_out, ram_1_data, ram_2_data,
       ram_3_data, registerfile_1_p4, registerfile_1_p14;
  wire [7:0] adder_1_out, adder_2_out, bit_extender_1_out, multiplexer_1_out, multiplexer_2_out, register_1_q;
  wire [11:4] ram_1_data_2;

  Register register_1 (.D(multiplexer_2_out), .Q(register_1_q), .clk(in_3), .clr(in_1));  // open: en
  Adder adder_1 (.a(register_1_q), .b(8'h1), .out(adder_1_out));  // open: cin, cout
  RAM #(.dataWidth(16), .bus("asynch")) ram_1 (
    .addr(register_1_q), .data({out_5, ram_1_data_2, ram_1_data}), .sel(1'b1), .ld(1'b1));  // open: clr
  Multiplexer #(.width(8), .enable("false")) multiplexer_1 (
    .in0(adder_1_out), .in1(adder_2_out), .out(multiplexer_1_out), .sel(branch_1_branch));
  Adder adder_2 (.a(adder_1_out), .b(bit_extender_1_out), .out(adder_2_out));  // open: cin, cout
  assign bit_extender_1_out = {{4{1'b0}}, ram_1_data};  // Bit_Extender bit_extender_1
  Multiplexer #(.width(8), .enable("false")) multiplexer_2 (
    .in0(multiplexer_1_out), .in1(ram_1_data_2), .out(multiplexer_2_out), .sel(main_1_p3));
  // control_unit_main main_1: pin names not known; wires that end beside it: ram_1_data, out_5, main_1_p3, main_1_p4, main_1_p5, main_1_p6, main_1_p7, main_1_p8, main_1_p9, main_1_p10, main_1_p11, main_1_p12
  Multiplexer #(.width(4), .enable("false")) multiplexer_3 (
    .in0(ram_1_data_2[7:4]), .in1(ram_1_data), .out(multiplexer_3_out), .sel(main_1_p12));
  branch branch_1 (.zero(main_2_p2), .beq(main_1_p6), .bne(main_1_p5), .branch(branch_1_branch));
  // RegisterFile registerfile_1: pin names not known; wires that end beside it: ram_1_data_2[11:8], ram_1_data_2[7:4], multiplexer_3_out, registerfile_1_p4, in_3, to, t1, main_1_p9, t2, t3, t4, sp, registerfile_1_p13, registerfile_1_p14, registerfile_1_p13
  Comparator #(.width(4)) comparator_1 (.a(ram_1_data_2[11:8]), .b(4'b0110), .eq(comparator_1_eq));  // open: gt, lt
  Multiplexer #(.width(4), .enable("false")) multiplexer_4 (
    .in0(registerfile_1_p14), .in1(ram_1_data), .out(multiplexer_4_out), .sel(main_1_p11));
  // _4bitALU_main main_2: pin names not known; wires that end beside it: multiplexer_4_out, main_2_p2, main_1_p4, main_2_p4
  not not_1 (not_1_out, comparator_1_eq);
  RAM #(.addrWidth(4), .dataWidth(4), .bus("separate")) ram_2 (
    .addr(main_2_p4), .din(registerfile_1_p14), .data(ram_2_data), .str(main_1_p7), .sel(not_1_out),
    .clk(in_3), .ld(main_1_p8), .clr(Data_Memory));
  RAM #(.addrWidth(4), .dataWidth(4), .bus("separate")) ram_3 (
    .addr(main_2_p4), .din(registerfile_1_p14), .data(ram_3_data), .str(main_1_p7), .sel(comparator_1_eq),
    .clk(in_3), .ld(main_1_p8), .clr(in_4));
  Multiplexer #(.width(4), .enable("false")) multiplexer_5 (
    .in0(main_2_p4), .in1(ram_2_data), .out(multiplexer_5_out), .sel(main_1_p10));
  Multiplexer #(.width(4), .enable("false")) multiplexer_6 (
    .in0(multiplexer_5_out), .in1(ram_3_data), .out(registerfile_1_p4), .sel(comparator_1_eq));

  // Notes on the sheet:
  //   Stack memory
endmodule

module branch (
  input  zero,
  input  beq,
  input  bne,
  output branch
);

  wire n7404_1_p1, n7408_1_p3, n7408_1_p6;

  // _7404 7404_1: pin names not known; wires that end beside it: n7404_1_p1, zero
  // _7408 7408_1: pin names not known; wires that end beside it: zero, beq, n7408_1_p3, n7404_1_p1, bne, n7408_1_p6
  // _7432 7432_1: pin names not known; wires that end beside it: branch, n7408_1_p3, n7408_1_p6
endmodule
